# Fritzing sketch pick & place (saved by Fritzing 0.9.9b)

parts:
  Part1 = Arduino Nano (Rev3.0) (ICSP)
  W5500_Module1 = W5500 Ethernet module [package="DIP (Dual Inline) [THT]"]
  Relay = RELAY [package=relay-g5q]
  U2 = Sharp PC817 [package=THT]
  LED1 = LED - 3mm [color="Red (633nm)" current=0.030 package="3 mm [THT]"]
  R4 = Resistor [tolerance=±5% resistance=100 power=0.25 package=THT]
  D1 = Diode [package=diode-1n4001]
  STEP_DOWN_5V = RioRand LM2596
  JP_24V_IN = Header 2 [package=molex-1x2_lock]
  R6 = Resistor [tolerance=±5% resistance=10k power=0.25 package=THT]
  JP_SERVO = Header 3 [package=molex-1x3_lock]
  JP_SENSOR = Header 3 [package=molex-1x3_lock]
  LED2 = LED - 3mm [color="Red (633nm)" current=0.030 package="3 mm [THT]"]
  U3 = Sharp PC817 [package=THT]
  JP_VALVE_Z = Header 3 [package=molex-1x3_lock]
  JP_VALVE_C = Header 3 [package=molex-1x3_lock]
  JP_LED = Header 2 [package=molex-1x2_lock]
  JP_END_1 = Header 2 [package=molex-1x2_lock]
  JP_END_2 = Header 2 [package=molex-1x2_lock]
  LED3 = LED - 3mm [color="Red (633nm)" current=0.030 package="3 mm [THT]"]
  R7 = Resistor [tolerance=±5% resistance=100 power=0.25 package=THT]

nets:
  GND: Part1.GND, W5500_Module1.GND, U2.Pin_2, STEP_DOWN_5V.Pin_4, R6.Pin_1, JP_SERVO.1, U3.Pin_2, JP_LED.1, JP_END_1.1, JP_END_2.1
  N1: Part1.D2, R7.Pin_0
  N2: Part1.D3, JP_SERVO.3
  N3: Part1.D4, JP_END_2.2
  N4: Part1.D5, JP_END_1.2
  N5: Part1.D6, R6.Pin_0, LED2.cathode
  N6: Part1.D7, R4.Pin_0
  N7: Part1.D10, W5500_Module1.SCS
  N8: Part1.D11/MOSI, W5500_Module1.MOSI
  N9: Part1.D12/MISO, W5500_Module1.MISO
  5V: Part1.5V, W5500_Module1.5V, Relay.MAIN, STEP_DOWN_5V.Pin_3, JP_SERVO.2, JP_LED.2
  N10: Part1.D13/SCK, W5500_Module1.SCLK
  N11: Relay.COIL2, D1.C, JP_SENSOR.3
  N12: Relay.NO, LED2.anode
  N13: Relay.COIL1, D1.A, STEP_DOWN_5V.Pin_2, JP_24V_IN.2, JP_SENSOR.1, JP_VALVE_Z.1, JP_VALVE_C.1
  N14: U2.Pin_1, LED1.cathode
  N15: U2.Pin_4, STEP_DOWN_5V.Pin_1, JP_24V_IN.1, JP_SENSOR.2, U3.Pin_4, JP_VALVE_Z.2, JP_VALVE_C.2
  N16: U2.Pin_3, JP_VALVE_Z.3
  N17: LED1.anode, R4.Pin_1
  N18: U3.Pin_1, LED3.cathode
  N19: U3.Pin_3, JP_VALVE_C.3
  N20: LED3.anode, R7.Pin_1

custom parts:
  W5500 Ethernet module: W5500 based SPI Ethernet module for Arduino, etc.
